# Fritzing sketch GyroAndGpsWeymouth (saved by Fritzing 0.9.3b)
breadboards: 1

parts:
  Base = Raspberry Pi 3 [part_number=RPI-3-V1.2]
  MPU = InvenSense MPU6050
  GPS1 = BN-180GPS [package=BN-180]
  Nano = Arduino Nano (Rev3.0)

nets:
  3V3: Base.3v3, GPS1.VCC
  N1: Base.GIPO15, GPS1.TX-O
  N2: Base.GIPO14, GPS1.RX-I
  GND: Base.GND, GPS1.GND
  VCC: MPU.VCC, Nano.5V
  GND_2: MPU.GND, Nano.GND
  N3: MPU.SCL, Nano.A5
  N4: MPU.SDA, Nano.A4

notes:
  USB cable between RasPi and Nano
  MPU 6050
  BN-189GPS
  Serial Connection between Pi and Nano via USB

custom parts:
  BN-180GPS: GPS Geekstory BN-180GPS
